# Fritzing sketch Quadcopter_6050 (saved by Fritzing 0.9.2b)
circuit board: 6.88566cm x 5.36311cm
breadboards: 1

parts:
  J1 = Basic Servo
  J2 = Basic Servo
  J3 = Basic Servo
  J4 = Basic Servo
  Quadcopter = Arduino Uno (Rev3)
  GY2 = MPU-6050 Board GY-521 [form="♀ (female)" package=THT]
  S1 = Pushbutton [package="[THT]"]
  LED1 = LED - 5mm [color="Red (633nm)" package="5 mm [THT]"]
  R1 = Resistor [tolerance=±5% resistance=220 package=THT]
  J5 = female pin header, 2 pins [form="♀ (female)"]

nets:
  GND: J1.gnd, J2.gnd, J3.gnd, J4.gnd, Quadcopter.GND, GY2.pin2, S1.Pin_3, S1.Pin_4, R1.Pin_0
  N1: J1.vcc, J5.pin1
  N2: J1.pulse, Quadcopter.D6_PWM
  N3: J2.pulse, Quadcopter.D9_PWM
  N4: J3.pulse, Quadcopter.D10_PWM/SS
  N5: J4.pulse, Quadcopter.D11_PWM/MOSI
  N6: Quadcopter.A4/SDA, GY2.pin4
  N7: Quadcopter.A5/SCL, GY2.pin3
  N8: Quadcopter.D13/SCK, LED1.anode
  N9: Quadcopter.D2, GY2.pin8
  N10: Quadcopter.RESET, S1.Pin_1, S1.Pin_2
  N11: Quadcopter.3V3, GY2.pin1
  N12: Quadcopter.VIN, J5.pin2
  N13: LED1.cathode, R1.Pin_1

notes:
  Amir Aliabadi

custom parts:
  MPU-6050 Board GY-521: Acelerometro y Giroscopio MPU-6050 Board GY-521
